# Fritzing sketch AVP (saved by Fritzing 0.9.3b)

parts:
  4x20_LCD_screen_w/Green_Screen1 = 4x20 LCD screen w/Green Screen
  kEYPAD_MATRICIAL_1 = KEYPAD 4x3
  LED1 = LED - 5mm [color="Green (570nm)" package="5 mm [THT]"]
  LED2 = LED - 5mm [color="Red (660nm)" package="5 mm [THT]"]
  R1 = Resistor [tolerance=±5% resistance=1k package=THT]
  R2 = Resistor [tolerance=±5% resistance=1k package=THT]
  Part1 = Arduino Mega 2560 (Rev3)
  J1 = Basic Servo
  J2 = Piezo Speaker
  LCM1602_IIC1 = LCM1602 IIC [part_number="LCM1602 IIC" chip_label="LCM1602 IIC" package="DIP (Dual Inline) [THT]"]

nets:
  VSS: 4x20_LCD_screen_w/Green_Screen1.VSS, LCM1602_IIC1.VSS
  VDD: 4x20_LCD_screen_w/Green_Screen1.VDD, LCM1602_IIC1.VDD
  N1: 4x20_LCD_screen_w/Green_Screen1.V0, LCM1602_IIC1.V0
  N2: 4x20_LCD_screen_w/Green_Screen1.RS, LCM1602_IIC1.RS
  N3: 4x20_LCD_screen_w/Green_Screen1.R/W, LCM1602_IIC1.RW
  N4: 4x20_LCD_screen_w/Green_Screen1.E, LCM1602_IIC1.E
  N5: 4x20_LCD_screen_w/Green_Screen1.DB0, LCM1602_IIC1.D0
  N6: 4x20_LCD_screen_w/Green_Screen1.DB1, LCM1602_IIC1.D1
  N7: 4x20_LCD_screen_w/Green_Screen1.DB2, LCM1602_IIC1.D2
  N8: 4x20_LCD_screen_w/Green_Screen1.DB3, LCM1602_IIC1.D3
  N9: 4x20_LCD_screen_w/Green_Screen1.DB4, LCM1602_IIC1.D4
  N10: 4x20_LCD_screen_w/Green_Screen1.DB5, LCM1602_IIC1.D5
  N11: 4x20_LCD_screen_w/Green_Screen1.DB6, LCM1602_IIC1.D6
  N12: 4x20_LCD_screen_w/Green_Screen1.DB7, LCM1602_IIC1.D7
  N13: 4x20_LCD_screen_w/Green_Screen1.LED+, LCM1602_IIC1.A
  N14: 4x20_LCD_screen_w/Green_Screen1.LED-, LCM1602_IIC1.K
  N15: kEYPAD_MATRICIAL_1.col1, Part1.D41
  N16: kEYPAD_MATRICIAL_1.arrow1, Part1.D43
  N17: kEYPAD_MATRICIAL_1.col2, Part1.D45
  N18: kEYPAD_MATRICIAL_1.arrow2, Part1.D47
  N19: kEYPAD_MATRICIAL_1.col3, Part1.D49
  N20: kEYPAD_MATRICIAL_1.arrow3, Part1.D51
  N21: kEYPAD_MATRICIAL_1.arrow4, Part1.D53
  GND: LED1.cathode, LED2.cathode, Part1.GND, J1.gnd, J2.pin1, LCM1602_IIC1.GND
  N22: LED1.anode, R1.Pin_1
  N23: LED2.anode, R2.Pin_1
  N24: R1.Pin_0, Part1.D8_PWM
  N25: R2.Pin_0, Part1.D7_PWM
  N26: Part1.D21/SCL, LCM1602_IIC1.SCL
  N27: Part1.D20/SDA, LCM1602_IIC1.SDA
  N28: Part1.D9_PWM, J1.pulse
  VCC: Part1.5V, J1.vcc, LCM1602_IIC1.VCC
  N29: Part1.D6_PWM, J2.pin2

custom parts:
  4x20 LCD screen w/Green Screen: A standard character display with 4x20 characters.
  KEYPAD 4x3: KEYPAD matricial de 12 botones, 4 filas x 3 columnas
  LCM1602 IIC: I2C-Module to use a 1602 or 2004 LCD on with the wire.h libory Serial LCD Modul
